// Logisim project Master.circ as structural Verilog: 1 circuit, main circuit main
module main (
);

  wire Add, and_2_out, and_5_out, clock_1_out, DReg_0, DReg_1, DReg_2, DReg_3, DReg_4, DReg_5, DReg_6,
       DReg_7, Group_0, Group_1, Group_2, Group_3, Group_4, HALT, Mul, not_1_out, not_2_out, not_3_out,
       not_4_out, not_5_out, not_6_out, not_7_out, not_8_out, not_9_out, not_10_out, not_11_out, not_12_out,
       not_13_out, not_14_out, not_15_out, or_1_out, or_2_out, or_3_out, or_4_out, RRMov, SReg_0, SReg_1,
       SReg_2, SReg_3, SReg_4, SReg_5, SReg_6, SReg_7, Sub, Subtract_On;
  wire [3:0] Group, Instruction;
  wire [4:0] counter_1_q;
  wire [7:0] Dest, R0, R1, R2, R3, R4, R5, R6, R7, RegA, RegB, Source;

  Counter #(.width(5), .max('h1f)) counter_1 (.Q(counter_1_q), .clk(clock_1_out));  // open: load, D, count, carry, clr
  Clock clock_1 (.out(clock_1_out));
  not not_1 (not_1_out, Group[1]);
  not not_2 (not_2_out, Group[2]);
  not not_3 (not_3_out, Group[3]);
  not not_4 (not_4_out, Group[0]);
  not not_5 (not_5_out, Group[1]);
  and and_1 (Group_0, not_4_out, not_5_out, not_2_out, not_3_out);
  LED led_1 (.in(Group_0));
  and and_2 (and_2_out, Group_3, Instruction[0], Instruction[1], ~Instruction[2], ~Instruction[3]);  // AND_Gate
  LED led_2 (.in(and_2_out));
  not not_6 (not_6_out, Group[2]);
  not not_7 (not_7_out, Group[3]);
  not not_8 (not_8_out, Group[2]);
  not not_9 (not_9_out, Group[0]);
  and and_3 (Group_1, Group[0], not_1_out, not_8_out, not_7_out);
  and and_4 (Group_2, not_9_out, Group[1], not_6_out, not_12_out);
  LED led_3 (.in(Group_1));
  LED led_4 (.in(Group_2));
  and and_5 (and_5_out, Group_3, ~Instruction[0], Instruction[1], Instruction[2], ~Instruction[3]);  // AND_Gate
  LED led_5 (.in(and_5_out));
  ROM #(.addrWidth(5), .dataWidth(24)) rom_1 (
    .addr(counter_1_q), .data({Group, Instruction, Source, Dest}));  // open: sel
  not not_10 (not_10_out, Group[2]);
  not not_11 (not_11_out, Group[3]);
  not not_12 (not_12_out, Group[3]);
  and and_6 (Group_3, Group[0], Group[1], not_10_out, not_11_out);
  LED led_6 (.in(Group_3));
  not not_13 (not_13_out, Group[0]);
  not not_14 (not_14_out, Group[3]);
  not not_15 (not_15_out, Group[1]);
  and and_7 (Group_4, not_13_out, not_15_out, Group[2], not_14_out);
  LED led_7 (.in(Group_4));
  and and_8 (Add, Group_2, Instruction[0], Instruction[1], Instruction[2], ~Instruction[3]);  // AND_Gate
  and and_9 (Mul, Group_2, Instruction[0], ~Instruction[1], ~Instruction[2], Instruction[3]);  // AND_Gate
  LED led_8 (.in(Mul));
  LED led_9 (.in(Add));
  and and_10 (RRMov, Group_2, ~Instruction[0], Instruction[1], ~Instruction[2], ~Instruction[3]);  // AND_Gate
  LED led_10 (.in(RRMov));
  or or_1 (or_1_out, Group_2, Group_4, Group_3);
  and and_11 (Sub, Group_2, ~Instruction[0], ~Instruction[1], ~Instruction[2]);  // AND_Gate
  LED led_11 (.in(Sub));
  and and_12 (SReg_0, ~Source[3], ~Source[2], ~Source[1], Source[0], or_1_out);  // AND_Gate
  and and_13 (SReg_1, ~Source[3], ~Source[2], Source[1], ~Source[0], or_1_out);  // AND_Gate
  LED led_12 (.in(SReg_0));
  LED led_13 (.in(SReg_1));
  or or_2 (or_2_out, Group_2, Group_4, Group_3);
  and and_14 (SReg_2, ~Source[3], ~Source[2], Source[1], Source[0], or_1_out);  // AND_Gate
  LED led_14 (.in(SReg_2));
  Decoder #(.select(4)) decoder_1 (
    .out0(HALT), .out8(Subtract_On), .sel(Instruction));  // open: out1, out2, out3, out4, out5, out6, out7, out9, out10, out11, out12, out13, out14, out15, en
  and and_15 (SReg_3, ~Source[3], Source[2], ~Source[1], ~Source[0], or_1_out);  // AND_Gate
  LED led_15 (.in(SReg_3));
  and and_16 (SReg_5, ~Source[3], Source[2], Source[1], ~Source[0], or_1_out);  // AND_Gate
  and and_17 (SReg_4, ~Source[3], Source[2], ~Source[1], Source[0], or_1_out);  // AND_Gate
  LED led_16 (.in(SReg_4));
  LED led_17 (.in(SReg_5));
  Multiplexer #(.select(4), .width(8)) multiplexer_1 (
    .in1(R0), .in2(R1), .in3(R2), .in4(R3), .in5(R4), .in6(R5), .in7(R6), .in8(R7), .out(RegA),
    .sel(Source[3:0]), .en(or_2_out));  // open: in0, in9, in10, in11, in12, in13, in14, in15
  and and_18 (SReg_6, ~Source[3], Source[2], Source[1], Source[0], or_1_out);  // AND_Gate
  LED led_18 (.in(SReg_6));
  and and_19 (SReg_7, Source[3], ~Source[2], ~Source[1], ~Source[0], or_1_out);  // AND_Gate
  LED led_19 (.in(SReg_7));
  or or_3 (or_3_out, Group_2, Group_1, Group_3);
  or or_4 (or_4_out, Group_2, Group_1, Group_3);
  and and_20 (DReg_0, ~Dest[3], ~Dest[2], ~Dest[1], Dest[0], or_3_out);  // AND_Gate
  LED led_20 (.in(DReg_0));
  and and_21 (DReg_2, ~Dest[3], ~Dest[2], Dest[1], Dest[0], or_3_out);  // AND_Gate
  and and_22 (DReg_1, ~Dest[3], ~Dest[2], Dest[1], ~Dest[0], or_3_out);  // AND_Gate
  LED led_21 (.in(DReg_2));
  LED led_22 (.in(DReg_1));
  Multiplexer #(.select(4), .width(8)) multiplexer_2 (
    .in1(R0), .in2(R1), .in3(R2), .in4(R3), .in5(R4), .in6(R5), .in7(R6), .in8(R7), .out(RegB),
    .sel(Dest[3:0]), .en(or_4_out));  // open: in0, in9, in10, in11, in12, in13, in14, in15
  and and_23 (DReg_3, ~Dest[3], Dest[2], ~Dest[1], ~Dest[0], or_3_out);  // AND_Gate
  LED led_23 (.in(DReg_3));
  and and_24 (DReg_4, ~Dest[3], Dest[2], ~Dest[1], Dest[0], or_3_out);  // AND_Gate
  LED led_24 (.in(DReg_4));
  and and_25 (DReg_5, ~Dest[3], Dest[2], Dest[1], ~Dest[0], or_3_out);  // AND_Gate
  and and_26 (DReg_6, ~Dest[3], Dest[2], Dest[1], Dest[0], or_3_out);  // AND_Gate
  LED led_25 (.in(DReg_5));
  LED led_26 (.in(DReg_6));
  and and_27 (DReg_7, Dest[3], ~Dest[2], ~Dest[1], ~Dest[0], or_3_out);  // AND_Gate
  LED led_27 (.in(DReg_7));

  // Notes on the sheet:
  //   halt
  //   ldm
  //   IRMov
  //   Instructions
  //   stm
  //   contents of rom_1 (hex, n*v repeats v):
  //   270102 290805 115c07 220604 4bff00 0 4a1b00 280301 330203 5407ab 360408 5505bf
  //   help
  //   Source
  //   Destination
endmodule
